// Logisim project logism1.circ as structural Verilog: 2 circuits, main circuit main
module main (
  input  [3:0] Input,
  output Output
);

  Hex_Digit_Display hex_digit_display_1 (.value(Input));  // open: dp
  subCircuit subcircuit_1 (.A(Input[0]), .B(Input[1]), .C(Input[2]), .D(Input[3]), .F(Output));
endmodule

module subCircuit (
  input  A,
  input  B,
  input  C,
  input  D,
  output F
);

  wire and_1_out, and_2_out, and_3_out, and_4_out, and_5_out, and_6_out, and_7_out, and_8_out, and_9_out,
       and_10_out, and_11_out, and_12_out, and_13_out, and_14_out, and_15_out, and_16_out, and_17_out,
       and_18_out, not_1_out, not_2_out, not_3_out, not_4_out, not_5_out, not_6_out, not_7_out, not_8_out,
       not_9_out, not_10_out, not_11_out, not_12_out, or_1_out, or_2_out, or_3_out, or_4_out;

  not not_1 (not_1_out, A);
  and and_1 (and_1_out, not_1_out, not_2_out);
  not not_2 (not_2_out, B);
  not not_3 (not_3_out, C);
  and and_2 (and_2_out, not_3_out, not_4_out);
  not not_4 (not_4_out, D);
  not not_5 (not_5_out, A);
  and and_3 (and_3_out, not_5_out, not_6_out);
  not not_6 (not_6_out, B);
  and and_4 (and_4_out, C, D);
  not not_7 (not_7_out, A);
  not not_8 (not_8_out, D);
  and and_5 (and_5_out, A, not_9_out);
  not not_9 (not_9_out, B);
  not not_10 (not_10_out, C);
  and and_6 (and_6_out, not_10_out, D);
  and and_7 (and_7_out, A, B);
  not not_11 (not_11_out, C);
  and and_8 (and_8_out, not_11_out, not_12_out);
  not not_12 (not_12_out, D);
  and and_9 (and_9_out, and_1_out, and_2_out);
  and and_10 (and_10_out, and_3_out, and_4_out);
  and and_11 (and_11_out, not_7_out, B);
  and and_12 (and_12_out, C, not_8_out);
  and and_13 (and_13_out, and_5_out, and_6_out);
  and and_14 (and_14_out, and_7_out, and_8_out);
  and and_15 (and_15_out, A, B);
  and and_16 (and_16_out, C, D);
  or or_1 (or_1_out, and_9_out, and_10_out);
  and and_17 (and_17_out, and_11_out, and_12_out);
  or or_2 (or_2_out, and_13_out, and_14_out);
  and and_18 (and_18_out, and_15_out, and_16_out);
  or or_3 (or_3_out, or_1_out, and_17_out);
  or or_4 (or_4_out, or_2_out, and_18_out);
  or or_5 (F, or_3_out, or_4_out);
endmodule
